# Fritzing sketch SF51-Server (saved by Fritzing 0.9.3b)
breadboards: 1

parts:
  J1 = MAGJACK [package=magjack]
  U1 = NodeMCU V3.0
  TRXCOM1 = RJ45-TRXCOM [part_number=TRJ0011BANL]
  U3 = AD22100 - Voltage Output Temperature Sensor with Signal Conditioning [part_number=AD22100]
  KY-1 = Keyes Relay [package=THT]
  KY-2 = Keyes Relay [package=THT]
  TRXCOM2 = RJ45-TRXCOM [part_number=TRJ0011BANL]
  R1 = Photocell (LDR) [package=THT]
  R2 = Photocell (LDR) [package=THT]
  Q2 = NPN-Transistor [package="TO92 [THT]"]
  Q3 = NPN-Transistor [package="TO92 [THT]"]
  R6 = Resistor [tolerance=±2% resistance=4.7k package=THT]
  R7 = Resistor [tolerance=±2% resistance=1k package=THT]
  R8 = Resistor [tolerance=±2% resistance=1k package=THT]
  C1 = Electrolytic Capacitor [capacitance=1µF package="100 mil [THT, electrolytic]"]

nets:
  N1: J1.SHIELD, U1.3V3, Q2.E, R6.Pin_1
  N2: J1.RD-, U1.GND#6, U1.GND#13, U1.GND#16, U1.GND#33, Q2.C, Q3.C, R7.Pin_0, R8.Pin_0, C1.-
  N3: J1.RCT, U1.D7, R8.Pin_1
  N4: U1.D1, Q2.B
  N5: U1.D2, Q3.B
  N6: U1.D5, R7.Pin_1
  N7: U1.D6, R6.Pin_0
  N8: U1.VU, C1.+
  N9: TRXCOM1.Receive_CT, KY-2.power
  N10: TRXCOM1.Receive_RD-, KY-2.signal
  N11: TRXCOM1.n.c., R2.pin_1
  N12: TRXCOM1.CHS_Ground, R2.pin_0
  N13: TRXCOM1.Green_Anode_+, KY-2.ground
  N14: U3.V+, R1.pin_1
  N15: U3.Vo, TRXCOM2.Transmit_TD-
  N16: U3.GND, KY-1.ground, TRXCOM2.Transmit_TD+
  N17: KY-1.signal, TRXCOM2.Yellow_Kathode_-
  N18: KY-1.power, TRXCOM2.Yellow_Anode_+
  N19: TRXCOM2.Transmit_CT, R1.pin_0

notes:
  Cool Server (Laptop)
  Strong Server Xeon
  Dallas Temperture sensor

custom parts:
  NodeMCU V3.0: ESP8266 based NodeMCU
  Keyes Relay: The Keyes 5V relay module is suitable for SCM development, home appliance control. It uses a 5V~12V TIL control signal which can control DC / AC signal.
